# Fritzing sketch ir_sender_sketch (saved by Fritzing 0.7.4b)
breadboards: 1

parts:
  Arduino1 = Arduino
  S1 = Pushbutton [package=THT]
  LED1 = LED - 5mm [color="Red (633nm)" package="5 mm [THT]"]
  R1 = Resistor [tolerance=±5% resistance=27 package=THT]
  Q1 = NPN-Transistor [package="TO92 [THT]"]
  R2 = Resistor [tolerance=±5% resistance=820 package=THT]
  R3 = Resistor [tolerance=±5% resistance=27 package=THT]
  LED2 = LED - 5mm [color="Infrared (940nm)" current=90mA package="5 mm [THT]"]

nets:
  N1: Arduino1.D13, R1.Pin_1
  N2: Arduino1.D3, R2.Pin_1
  N3: Arduino1.D2, S1.leg0
  N4: Arduino1.+5V, LED2.cathode
  N5: Arduino1.GND, S1.leg1, LED1.cathode, Q1.C
  N6: LED1.anode, R1.Pin_0
  N7: Q1.E, R3.Pin_1
  N8: Q1.B, R2.Pin_0
  N9: R3.Pin_0, LED2.anode
