# Fritzing sketch stopwatch_sketch (saved by Fritzing 0.7.4b)
breadboards: 1

parts:
  LCD1 = LCD screen
  R1 = Rotary Potentiometer (Small) [maximum_resistance=10kΩ]
  LED1 = LED - 5mm [color="Red (633nm)" package="5 mm [THT]"]
  R2 = Resistor [tolerance=±5% resistance=220 package=THT]
  S1_Start/Stop = Pushbutton [package=THT]
  S2_Reset = Pushbutton [package=THT]
  Arduino1 = Arduino
  Bauteil1 = IR Receiver Breakout [package=PCB]

nets:
  GND: LCD1.VSS, LCD1.R/W, LCD1.LED-, R1.leg2, LED1.cathode, S1_Start/Stop.leg1, S2_Reset.leg1, Arduino1.GND, Bauteil1.GND
  VDD: LCD1.VDD, LCD1.LED+, R1.leg1, Arduino1.+5V, Bauteil1.VCC
  N1: LCD1.V0, R1.wiper
  N2: LCD1.RS, Arduino1.D12
  N3: LCD1.E, Arduino1.D11
  N4: LCD1.DB4, Arduino1.D5
  N5: LCD1.DB5, Arduino1.D4
  N6: LCD1.DB6, Arduino1.D3
  N7: LCD1.DB7, Arduino1.D2
  N8: LED1.anode, R2.Pin_0
  N9: R2.Pin_1, Arduino1.D10
  N10: S1_Start/Stop.leg0, Arduino1.D6, Bauteil1.OUT
  N11: S2_Reset.leg0, Arduino1.D7
